# Fritzing sketch button_with_led (saved by Fritzing 0.9.3b)
breadboards: 1

parts:
  Part1 = Arduino Nano (Rev3.0)
  LED1 = smd LED [color="Red (633nm)" package="0805 [SMD]"]
  R1 = Resistor [tolerance=±5% resistance=330 package="2512 [SMD]"]
  S1 = Pushbutton [package="[THT]"]
  R2 = Resistor [tolerance=±5% resistance=10k package="2512 [SMD]"]

nets:
  N1: Part1.GND, LED1.cathode, R2.Pin_1
  N2: Part1.D2, S1.Pin_1, S1.Pin_2, R2.Pin_0
  N3: Part1.D8, R1.Pin_0
  N4: Part1.5V, S1.Pin_3, S1.Pin_4
  N5: LED1.anode, R1.Pin_1
