# Fritzing sketch schematic (saved by Fritzing 0.9.3b)
breadboards: 1

parts:
  Part1 = Arduino Nano (Rev3.0) (ICSP)
  Part3 = LCD1602-I2C

nets:
  GND: Part1.GND, Part3.GND
  5V: Part1.5V, Part3.VCC
  N1: Part1.A5, Part3.SCL
  N2: Part1.A4, Part3.SDA

custom parts:
  LCD1602-I2C: A standard character display, usually with 2x16 characters. Comes in many colors with LCM1602 IIC attached.
