# Fritzing sketch Untitled Sketch (saved by Fritzing 0.9.3b)

parts:
  Part1 = Arduino Nano (Rev3.0)
  8x8_LED_Modul_mit_MAX1 = 8x8 LED Modul mit MAX7219 [package=THT]
  8x8_LED_Modul_mit_MAX2 = 8x8 LED Modul mit MAX7219 [package=THT]
  8x8_LED_Modul_mit_MAX3 = 8x8 LED Modul mit MAX7219 [package=THT]
  8x8_LED_Modul_mit_MAX4 = 8x8 LED Modul mit MAX7219 [package=THT]
  ZS-042_RTC1 = ZS-042 RTC Module

nets:
  N1: Part1.GND, 8x8_LED_Modul_mit_MAX1.GND_Eingang
  N2: Part1.D10, 8x8_LED_Modul_mit_MAX1.CS_Eingang
  N3: Part1.D11/MOSI, 8x8_LED_Modul_mit_MAX1.DIN_Eingang
  5V: Part1.5V, 8x8_LED_Modul_mit_MAX1.VCC_Eingang, ZS-042_RTC1.VCC
  N4: Part1.A5, ZS-042_RTC1.SCL
  N5: Part1.A4, ZS-042_RTC1.SDA
  N6: Part1.D13/SCK, 8x8_LED_Modul_mit_MAX1.CLK_Eingang
  N7: 8x8_LED_Modul_mit_MAX1.VCC_Ausgang, 8x8_LED_Modul_mit_MAX2.VCC_Eingang
  N8: 8x8_LED_Modul_mit_MAX1.GND_Ausgang, 8x8_LED_Modul_mit_MAX2.GND_Eingang
  N9: 8x8_LED_Modul_mit_MAX1.DOUT_Ausgang, 8x8_LED_Modul_mit_MAX2.DIN_Eingang
  N10: 8x8_LED_Modul_mit_MAX1.CS_Ausgang, 8x8_LED_Modul_mit_MAX2.CS_Eingang
  N11: 8x8_LED_Modul_mit_MAX1.CLK_Ausgang, 8x8_LED_Modul_mit_MAX2.CLK_Eingang
  N12: 8x8_LED_Modul_mit_MAX2.VCC_Ausgang, 8x8_LED_Modul_mit_MAX3.VCC_Eingang
  N13: 8x8_LED_Modul_mit_MAX2.GND_Ausgang, 8x8_LED_Modul_mit_MAX3.GND_Eingang
  N14: 8x8_LED_Modul_mit_MAX2.DOUT_Ausgang, 8x8_LED_Modul_mit_MAX3.DIN_Eingang
  N15: 8x8_LED_Modul_mit_MAX2.CS_Ausgang, 8x8_LED_Modul_mit_MAX3.CS_Eingang
  N16: 8x8_LED_Modul_mit_MAX2.CLK_Ausgang, 8x8_LED_Modul_mit_MAX3.CLK_Eingang
  N17: 8x8_LED_Modul_mit_MAX3.VCC_Ausgang, 8x8_LED_Modul_mit_MAX4.VCC_Eingang
  N18: 8x8_LED_Modul_mit_MAX3.GND_Ausgang, 8x8_LED_Modul_mit_MAX4.GND_Eingang
  N19: 8x8_LED_Modul_mit_MAX3.DOUT_Ausgang, 8x8_LED_Modul_mit_MAX4.DIN_Eingang
  N20: 8x8_LED_Modul_mit_MAX3.CS_Ausgang, 8x8_LED_Modul_mit_MAX4.CS_Eingang
  N21: 8x8_LED_Modul_mit_MAX3.CLK_Ausgang, 8x8_LED_Modul_mit_MAX4.CLK_Eingang
