# Fritzing sketch schematic i2c master and slave (saved by Fritzing 0.9.3b)

parts:
  Part1 = Arduino Nano (Rev3.0) (ICSP)
  Part2 = Arduino Nano (Rev3.0) (ICSP)

nets:
  N1: Part1.A5, Part2.A5
  N2: Part1.A4, Part2.A4

notes:
  SDA-> A4
  SCL -> A5
