# Fritzing sketch schematic (saved by Fritzing 0.9.3b)

parts:
  Part1 = Arduino Nano (Rev3.0)
  o1 = Module display OLED I2C 128x64 SSD1306 [package=THT]
  Mod1 = KY-023 Dual Axis Joystick Module [package="Breakout board"]

nets:
  N1: Part1.D2, Mod1.SW
  VIN: Part1.VIN, Mod1.+5V
  GND: Part1.GND, o1.GND, Mod1.GND
  N2: Part1.A5, o1.SCL
  N3: Part1.A4, o1.SDA
  N4: Part1.A1, Mod1.VRy
  N5: Part1.A0, Mod1.VRx
  3V3: Part1.3V3, o1.VCC

custom parts:
  Module display OLED I2C 128x64 SSD1306: Ecran OLED I2C SSD163 de 128x64 avec connexion I2C
  KY-023 Dual Axis Joystick Module: KY-023 Dual-Axis Joystick Module.
