# Fritzing sketch schematic (saved by Fritzing 0.9.3b)

parts:
  Part1 = Arduino Nano (Rev3.0) (ICSP)
  U1 = WS2812 RGB LED strip

nets:
  N1: Part1.D6, U1.DIN
  GND: Part1.GND, U1.GND
  5V: Part1.5V, U1.VCC

custom parts:
  WS2812 RGB LED strip: WS2812 strip
